# Fritzing sketch alles (saved by Fritzing 0.9.5d)
circuit board: 2.32356cm x 1.15517cm
perfboards: 1

parts:
  part = female pin header, 7 pins [form="♀ (female)"]
  J1 = female pin header, 9 pins [form="♀ (female)"]

nets:
  N1: part.pin1, J1.pin8
  N2: part.pin2, J1.pin7
  N3: part.pin3, J1.pin6
  N4: part.pin4, part.pin7, J1.pin1
  N5: part.pin6, J1.pin2

notes:
  alles
